# Fritzing sketch Design_2 (saved by Fritzing 0.8.7b)
breadboards: 1

parts:
  M1 = 5-ir-array-sensor [package=THT]
  Part1 = Adafruit PowerBoost 1000C [part_number="Adafruit #2465"]
  BATT1 = LiPoly Battery (1300mAh)
  M2 = DC Motor
  M4 = DC Motor
  X1 = USB Connectors [package=usb-a-h]
  BATT2 = LiPoly Battery (1300mAh)
  S1 = SWITCH-MOMENTARY-2 [package=tactile-switch-1101ne]
  S2 = SWITCH-MOMENTARY-2 [package=tactile-switch-1101ne]
  Mod1 = SparkFun_Auto_pHAT

nets:
  N1: M1.S5, Mod1.GPIO26
  N2: M1.S4, Mod1.GPIO19
  N3: M1.S3, Mod1.GPIO13
  N4: M1.S2, Mod1.GPIO6
  GND: M1.S1, M1.GND, Part1.GND, X1.GND, BATT2.negative, Mod1.GND-6, Mod1.GPIO5, Mod1.GND-30, Mod1.GND-39
  N5: M1.VCC, Mod1.GPIO9
  N6: Part1.VBUS, X1.D+, S2.1
  N7: Part1.VLIPO, BATT1.positive
  N8: Part1.ENABLE, BATT1.negative
  N9: Part1.5.0V, S1.2
  N10: M2.pin_1, M2.pin_2, M4.pin_1, M4.pin_2, BATT2.positive, S2.2, Mod1.AOUT1, Mod1.AOUT2, Mod1.BOUT1, Mod1.BOUT2
  N11: S1.1, Mod1.5V-4

custom parts:
  5-ir-array-sensor: 5 IR array sensor.
  Adafruit PowerBoost 1000C: PowerBoost 1000C is the perfect power supply for your portable project! With a built-in load-sharing battery charger circuit, you'll be able to keep your power-hungry project running even while recharging the battery! This little DC/DC boost converter module can be powered by any 3.7V LiIon/LiPoly battery, and convert the battery output to 5.2V DC for running your 5V projects.
  LiPoly Battery (1300mAh): Lithium Ion Polymer Battery (1300mAh)
  SparkFun_Auto_pHAT: Sparkfun SparkFun_Auto_pHAT Raspberry PI hat.
